# Fritzing sketch HW_SCHEMATICS (saved by Fritzing 0.9.5d)
breadboards: 1

parts:
  Part1 = Arduino Uno (Rev3) - ICSP
  Disp1 = LBT2088AH [part_number=LBT2088AH]  # not connected
  Disp2 = LBT2088AH [part_number=LBT2088AH]  # not connected
  Disp3 = LBT2088AH [part_number=LBT2088AH]  # not connected
  Disp4 = LBT2088AH [part_number=LBT2088AH]  # not connected
  J1 = Piezo Speaker
  S1 = Pushbutton [package="[THT]"]
  S2 = Pushbutton [package="[THT]"]
  R1 = Resistor [tolerance=±5% resistance=10k package="2512 [SMD]"]
  R2 = Resistor [tolerance=±5% resistance=10k package="2512 [SMD]"]
  R3 = Resistor [tolerance=±5% resistance=100 package="0603 [SMD]"]

nets:
  N1: Part1.D9_PWM, R3.Pin_0
  N2: Part1.D2, S2.Pin_1, S2.Pin_2, R1.Pin_0
  N3: Part1.D4, S1.Pin_1, S1.Pin_2, R2.Pin_0
  N4: Part1.5V, S1.Pin_3, S1.Pin_4, S2.Pin_3, S2.Pin_4
  N5: Part1.GND, J1.pin1, R1.Pin_1, R2.Pin_1
  N6: J1.pin2, R3.Pin_1

notes:
  CS
  CLK
  DIN
  VCC
  GND
